# Fritzing sketch BaseDisplay (saved by Fritzing 0.9.4)
breadboards: 1

parts:
  Part1 = Arduino Nano (Rev3.0)
  U1 = MAX7219 [package=dil24]  # not connected
  R1 = Resistor [tolerance=±5% resistance=1k package=THT]
  Q1 = NPN-Transistor [part_number=2N2222 package="TO92 [THT]"]
  Q2 = NPN-Transistor [part_number=2N2222 package="TO92 [THT]"]
  R2 = Resistor [tolerance=±5% resistance=1k package=THT]
  R3 = Resistor [tolerance=±5% resistance=1k package=THT]
  R4 = Resistor [tolerance=±5% resistance=1k package=THT]
  R5 = Resistor [tolerance=±5% resistance=1k package=THT]
  Q3 = NPN-Transistor [part_number=2N2222 package="TO92 [THT]"]
  Q5 = NPN-Transistor [part_number=2N2222 package="TO92 [THT]"]
  R6 = Resistor [tolerance=±5% resistance=330 package=THT]
  R7 = Resistor [tolerance=±5% resistance=330 package=THT]
  R8 = Resistor [tolerance=±5% resistance=330 package=THT]
  R9 = Resistor [tolerance=±5% resistance=330 package=THT]
  R10 = Resistor [tolerance=±5% resistance=330 package=THT]
  R11 = Resistor [tolerance=±5% resistance=330 package=THT]
  R12 = Resistor [tolerance=±5% resistance=330 package=THT]
  Q4 = NPN-Transistor [package="TO92 [THT]"]

nets:
  N1: Part1.GND, Q1.E, Q2.E, R3.Pin_1, Q3.B, Q5.E, Q4.E
  N2: Part1.D2, R7.Pin_1
  N3: Part1.D3, R6.Pin_1
  N4: Part1.D4, R12.Pin_1
  N5: Part1.D5, R11.Pin_1
  N6: Part1.D6, R10.Pin_1
  N7: Part1.D8, R9.Pin_1
  N8: Part1.D9, R8.Pin_1
  N9: Part1.D11/MOSI, R4.Pin_1
  N10: Part1.D12/MISO, R5.Pin_1
  N11: Part1.A3, R1.Pin_0
  N12: Part1.A2, R2.Pin_0
  N13: Part1.A1, R3.Pin_0
  N14: R1.Pin_1, Q1.B
  N15: Q2.B, R2.Pin_1
  N16: R4.Pin_0, Q4.B
  N17: R5.Pin_0, Q5.B
